# Fritzing sketch water_pump (saved by Fritzing 0.9.9b)
breadboards: 1

parts:
  Argon2 = Particle Argon
  OLED_I2C1 = OLED 128x64 I2C Monochrome Display
  Q1 = PNP-Transistor [package="TO92 [THT]"]
  R1 = Resistor [tolerance=±5% power=0.25 resistance=2.2k package=THT]
  R2 = Resistor [tolerance=±5% power=0.25 resistance=47 package=THT]
  Relay1 = Relay - 6 pins [package="DIP (Dual Inline) [THT]"]
  WATER_PUMP1 = water pump/motor  # not connected

nets:
  3.3V: Argon2.3.3V, OLED_I2C1.VDD, R2.Pin_0, Relay1.VCC, Relay1.ON
  GND: Argon2.GND, OLED_I2C1.GND, Q1.C, R1.Pin_1, Relay1.GND
  N1: Argon2.A0, OLED_I2C1.SCK
  N2: Argon2.A1, OLED_I2C1.SDA
  N3: Argon2.MI, Q1.B, R1.Pin_0
  N4: Q1.E, R2.Pin_1, Relay1.IN

custom parts:
  Particle Argon: The Argon is a powerful Wi-Fi enabled development board that can act as either a standalone Wi-Fi endpoint or Wi-Fi enabled gateway for Particle Mesh networks. It is based on the Nordic nRF52840 and has built-in battery charging circuitry so it’s easy to connect a Li-Po and deploy your local network in minutes. The Argon is great for connecting existing projects to the Particle Device Cloud or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
  Relay - 6 pins: A DIP stand-in part for whatever IC you want. With 6 pins on a 900mil dual inline package (DIP) footprint.
  water pump/motor: WATER PUMP BY ARDUBLOCKTR
